# Fritzing sketch LaserPointer (saved by Fritzing 0.8.7b)
circuit board: 7cm x 5cm
breadboards: 1

parts:
  74HC595_(LCD) = 74HC595 [package="DIP16 [THT]"]
  Yaw = female pin header, 6 pins [form="♀ (female)"]
  Pitch = female pin header, 6 pins [form="♀ (female)"]
  LCD1 = female pin header, 6 pins [form="♀ (female)"]
  LCD = female pin header, 6 pins [form="♀ (female)"]
  microSD1 = MicroSD Breakout
  XTAL1 = Crystal [frequency="16 Mhz" package=THT]
  C1 = Ceramic Capacitor [capacitance=0.22mF package="100 mil [THT, multilayer]"]
  C2 = Ceramic Capacitor [capacitance=0.22mF package="100 mil [THT, multilayer]"]
  Power_plug1 = Power plug
  U1 = atmega328 [package=dip]
  R1 = Resistor [tolerance=±5% resistance=10k package=THT]
  C3 = Electrolytic Capacitor [capacitance=1µF package="100 mil [THT, electrolytic]"]
  R2 = TRIMPOT [package=trimpot_pth_s3_lock]
  B1 = female pin header, 2 pins [form="♀ (female)"]
  R3 = Resistor [tolerance=±5% resistance=220 package=THT]
  B2 = female pin header, 2 pins [form="♀ (female)"]
  E1 = female pin header, 2 pins [form="♀ (female)"]
  E2 = female pin header, 2 pins [form="♀ (female)"]
  RESET = Pushbutton [package="[THT]"]
  L = female pin header, 2 pins [form="♀ (female)"]

nets:
  N1: 74HC595_(LCD).Q1, LCD.pin4
  N2: 74HC595_(LCD).Q3, LCD.pin6
  N3: 74HC595_(LCD).Q4, LCD1.pin1
  N4: 74HC595_(LCD).Q5, LCD1.pin2
  N5: 74HC595_(LCD).Q6, LCD1.pin3
  N6: 74HC595_(LCD).Q7, LCD1.pin4
  GND: 74HC595_(LCD).GND, microSD1.GND, C1.0, C2.0, Power_plug1.GND, U1.GND, C3.-, B1.pin2, B2.pin2, E1.pin2, E2.pin2, RESET.Pin_1, RESET.Pin_2, L.pin2
  VCC: 74HC595_(LCD).MR, 74HC595_(LCD).VCC, Yaw.pin6, Pitch.pin6, LCD1.pin5, LCD.pin2, microSD1.5V, Power_plug1.VCC, U1.VCC, U1.AVCC, U1.AREF, R1.Pin_0, C3.+, R2.CCW
  N7: 74HC595_(LCD).SH_CP, microSD1.CLK, U1.D13
  N8: 74HC595_(LCD).ST_CP, U1.A0
  N9: 74HC595_(LCD).DS, microSD1.DI, U1.D11_(PWM)
  N10: Yaw.pin1, Pitch.pin1
  N11: Yaw.pin2, U1.D9_(PWM)
  N12: Yaw.pin3, U1.D8
  N13: Yaw.pin4, U1.D7
  N14: Yaw.pin5, U1.D6_(PWM)
  N15: Pitch.pin2, U1.D5_(PWM)
  N16: Pitch.pin3, U1.D4
  N17: Pitch.pin4, U1.D3_(PWM)
  N18: Pitch.pin5, U1.D2
  N19: LCD1.pin6, R3.Pin_1
  N20: LCD.pin1, LCD.pin5, R2.CW, R3.Pin_0
  N21: LCD.pin3, R2.WIPER
  N22: microSD1.CS, U1.D10_(PWM)
  N23: microSD1.DO, U1.D12
  N24: XTAL1.pin_0, C2.1, U1.XLAT1
  N25: XTAL1.pin_1, C1.1, U1.XLAT2
  N26: U1.RESET, R1.Pin_1, RESET.Pin_3, RESET.Pin_4
  N27: U1.A1, E2.pin1
  N28: U1.A2, E1.pin1
  N29: U1.A3, B2.pin1
  N30: U1.A4, B1.pin1
  N31: U1.A5, L.pin1

notes:
  5v
  GND(1)
  Cont
  RS
  En
  DB4
  DB5
  DB7
  LX+
  DB6
  LX-
  4
  GND
  2
  1
  3
  (GND) RW
  -+

custom parts:
  MicroSD Breakout: 5V-ready microSD Breakout with Level Shifter
